// Logisim project TP2.circ as structural Verilog
module Decoder (
  input  F0,
  input  F1,
  output S0,
  output S1,
  output S2,
  output S3
);

  wire not_1_out, not_2_out, not_3_out, not_4_out;

  not not_1 (not_1_out, F0);
  not not_2 (not_2_out, F1);
  not not_3 (not_3_out, F0);
  not not_4 (not_4_out, F1);
  and and_1 (S0, not_1_out, not_2_out);
  and and_2 (S1, not_3_out, F1);
  and and_3 (S2, F0, not_4_out);
  and and_4 (S3, F0, F1);

  // Notes on the sheet:
  //   Décodeur 2 vers 4
endmodule

module FullAdder1bit (
  input  Carry_in,
  input  B,
  input  A,
  input  Enable,
  output Sum,
  output Carry_out
);

  wire and_1_out, and_2_out, xor_1_out, xor_2_out;

  and and_1 (and_1_out, Enable, A, B);
  xor xor_1 (xor_1_out, B, A);
  and and_2 (and_2_out, Enable, xor_1_out, Carry_in);
  or or_1 (Carry_out, and_1_out, and_2_out);
  xor xor_2 (xor_2_out, Carry_in, xor_1_out);
  and and_3 (Sum, xor_2_out, Enable);

  // Notes on the sheet:
  //   Additionneur complet à 1 bit de sortie
endmodule

module LogicalUnit (
  input  A,
  input  B,
  input  Enable_AB,
  input  Enable_A_B,
  input  Enable_Not_B,
  output AB,
  output A_B,
  output Not_B
);

  wire A_B_out, AB_out, Not_B_out;

  and u_AB (AB_out, A, B);
  or u_A_B (A_B_out, A, B);
  not u_Not_B (Not_B_out, B);
  and and_1 (AB, AB_out, Enable_AB);
  and and_2 (A_B, A_B_out, Enable_A_B);
  and and_3 (Not_B, Not_B_out, Enable_Not_B);

  // Notes on the sheet:
  //   Unité logique
endmodule

module ALU1bit (
  input  Carry_in,
  input  INVA,
  input  A,
  input  ENA,
  input  B,
  input  ENB,
  input  F0,
  input  F1,
  output Output,
  output Carry_out
);

  wire and_1_out, and_2_out, Decoder_s0, Decoder_s1, Decoder_s2, Decoder_s3, Full_adder_sum,
       Logical_unit_a_b, Logical_unit_ab, Logical_unit_not_b, xor_1_out;

  and and_1 (and_1_out, A, ENA);
  and and_2 (and_2_out, B, ENB);
  xor xor_1 (xor_1_out, INVA, and_1_out);
  Decoder Decoder (.F0(F0), .F1(F1), .S0(Decoder_s0), .S1(Decoder_s1), .S2(Decoder_s2), .S3(Decoder_s3));
  LogicalUnit Logical_unit (
    .A(xor_1_out), .B(and_2_out), .Enable_AB(Decoder_s0), .Enable_A_B(Decoder_s1), .Enable_Not_B(Decoder_s2),
    .AB(Logical_unit_ab), .A_B(Logical_unit_a_b), .Not_B(Logical_unit_not_b));
  FullAdder1bit Full_adder (
    .B(and_2_out), .A(xor_1_out), .Enable(Decoder_s3), .Carry_in(Carry_in), .Carry_out(Carry_out),
    .Sum(Full_adder_sum));
  or or_1 (Output, Logical_unit_ab, Logical_unit_a_b, Logical_unit_not_b, Full_adder_sum);

  // Notes on the sheet:
  //   Unité arithmétique et logique à 1 bit de sortie
  //   Sum
endmodule

module FullAdder3 (
  input  C,
  input  Carry_in,
  input  A,
  input  B,
  output Sum,
  output C0,
  output C1,
  output C2
);

  wire xor_1_out, xor_2_out;

  and and_1 (C0, B, A);
  xor xor_1 (xor_1_out, C, Carry_in);
  and and_2 (C1, Carry_in, C);
  xor xor_2 (xor_2_out, A, B);
  and and_3 (C2, xor_2_out, xor_1_out);
  xor xor_3 (Sum, xor_1_out, xor_2_out);

  // Notes on the sheet:
  //   Additionneur pour réaliser l'opération A + B +C + 1
  //   Principe: Additionner les 4 entrées en les prenant deux à deux pour obtenir une seule sortie, en conservant les éventuelles retenues
endmodule

module Mult3x1 (
  input  A2,
  input  A1,
  input  A0,
  input  B0,
  output S2,
  output S1,
  output S0
);

  and B0A2 (S2, A2, B0);
  and B0A1 (S1, A1, B0);
  and B0A0 (S0, A0, B0);

  // Notes on the sheet:
  //   Multiplicateur 3x1
endmodule

module Mult3x3 (
  input  A2,
  input  A1,
  input  A0,
  input  B2,
  input  B1,
  input  B0,
  output S5,
  output S4,
  output S3,
  output S2,
  output S1,
  output S0
);

  wire fulladder1bit_1_carry_out, fulladder1bit_2_carry_out, fulladder1bit_3_carry_out, fulladder3_1_c0,
       fulladder3_1_c1, fulladder3_1_c2, fulladder3_1_sum, fulladder3_2_c0, fulladder3_2_c1, fulladder3_2_c2,
       fulladder3_2_sum, fulladder3_3_c0, fulladder3_3_c1, fulladder3_3_c2, Mult3x1_2_s0, Mult3x1_2_s1,
       Mult3x1_2_s2, Mult3x1_3_s0, Mult3x1_3_s1, Mult3x1_3_s2, Mult3x1_s1, Mult3x1_s2;

  Mult3x1 Mult3x1 (.A2(A2), .A1(A1), .A0(A0), .B0(B0), .S2(Mult3x1_s2), .S1(Mult3x1_s1), .S0(S0));
  Mult3x1 Mult3x1_2 (.A2(A2), .A1(A1), .A0(A0), .B0(B1), .S2(Mult3x1_2_s2), .S1(Mult3x1_2_s1), .S0(Mult3x1_2_s0));
  Mult3x1 Mult3x1_3 (.A2(A2), .A1(A1), .A0(A0), .B0(B2), .S2(Mult3x1_3_s2), .S1(Mult3x1_3_s1), .S0(Mult3x1_3_s0));
  FullAdder3 fulladder3_1 (
    .C(fulladder3_2_c2), .Carry_in(fulladder3_2_c1), .A(fulladder3_2_c0), .B(Mult3x1_3_s2),
    .C0(fulladder3_1_c0), .C1(fulladder3_1_c1), .C2(fulladder3_1_c2), .Sum(fulladder3_1_sum));
  or or_1 (S5, fulladder3_1_c0, fulladder3_1_c1, fulladder3_1_c2, fulladder1bit_3_carry_out);
  FullAdder1bit fulladder1bit_1 (
    .B(Mult3x1_s1), .A(Mult3x1_2_s0), .Enable(1'b1), .Carry_in(1'b0), .Carry_out(fulladder1bit_1_carry_out),
    .Sum(S1));
  FullAdder3 fulladder3_2 (
    .C(fulladder3_3_c2), .Carry_in(fulladder3_3_c1), .A(fulladder3_3_c0), .B(Mult3x1_2_s2),
    .C0(fulladder3_2_c0), .C1(fulladder3_2_c1), .C2(fulladder3_2_c2), .Sum(fulladder3_2_sum));
  FullAdder1bit fulladder1bit_2 (
    .B(fulladder3_2_sum), .A(Mult3x1_3_s1), .Enable(1'b1), .Carry_in(1'b0),
    .Carry_out(fulladder1bit_2_carry_out), .Sum(S3));
  FullAdder1bit fulladder1bit_3 (
    .B(fulladder1bit_2_carry_out), .A(fulladder3_1_sum), .Enable(1'b1), .Carry_in(1'b0),
    .Carry_out(fulladder1bit_3_carry_out), .Sum(S4));
  FullAdder3 fulladder3_3 (
    .C(fulladder1bit_1_carry_out), .Carry_in(Mult3x1_s2), .A(Mult3x1_2_s1), .B(Mult3x1_3_s0),
    .C0(fulladder3_3_c0), .C1(fulladder3_3_c1), .C2(fulladder3_3_c2), .Sum(S2));

  // Notes on the sheet:
  //   Multiplicateur 3x3
  //   FullAdder3
  //   FullAdder1bit
  //   FullAdder1bit
  //   FullAdder3
  //   FullAdder3
  //   FullAdder1bit
endmodule

module ALU3bits (
  input  INVA,
  input  ENA,
  input  ENB,
  input  A2,
  input  A1,
  input  A0,
  input  Carry_in,
  input  B2,
  input  B1,
  input  B0,
  input  F0,
  input  F1,
  output Carry_out,
  output S2,
  output S1,
  output S0
);

  wire alu1bit_1_carry_out, alu1bit_2_carry_out;

  ALU1bit alu1bit_1 (
    .INVA(INVA), .A(A0), .ENA(ENA), .B(B0), .ENB(ENB), .F0(F0), .F1(F1), .Carry_in(Carry_in),
    .Carry_out(alu1bit_1_carry_out), .Output(S0));
  ALU1bit alu1bit_2 (
    .INVA(INVA), .A(A1), .ENA(ENA), .B(B1), .ENB(ENB), .F0(F0), .F1(F1), .Carry_in(alu1bit_1_carry_out),
    .Carry_out(alu1bit_2_carry_out), .Output(S1));
  ALU1bit alu1bit_3 (
    .INVA(INVA), .A(A2), .ENA(ENA), .B(B2), .ENB(ENB), .F0(F0), .F1(F1), .Carry_in(alu1bit_2_carry_out),
    .Carry_out(Carry_out), .Output(S2));
endmodule
